# Fritzing sketch kontti (saved by Fritzing 0.9.3b)
breadboards: 1

parts:
  RHT1 = Humidity and Temperature Sensor RHT03
  Part1 = Arduino Uno (Rev3)
  Raspberry_Pi_1 = Raspberry Pi 3 [part_number=RPI-3-V1.2]  # not connected
  T1 = LM35 Temperature Sensor [package="TO92 [THT]"]
  T2 = LM35 Temperature Sensor [package="TO92 [THT]"]
  Lights_relay = OMRON PCB Power Relay – G5LE [part_number="G5LE-1\n" package=THT]
  Pump_relay = OMRON PCB Power Relay – G5LE [part_number="G5LE-1\n" package=THT]
  wlevel_sensor_R1 = Resistor [tolerance=±5% resistance=2.2k package="0603 [SMD]"]
  wlevel_sensor_R2 = Resistor [tolerance=±5% resistance=2.2k package="0603 [SMD]"]
  DTH22_resistor = Resistor [tolerance=±5% resistance=10k package="0603 [SMD]"]

nets:
  VCC: RHT1.Vcc, Part1.5V, T1.Vout, T2.Vout, DTH22_resistor.Pin_1
  N1: RHT1.Data-signal, Part1.D4, DTH22_resistor.Pin_0
  N2: RHT1.GND_1, Part1.GND, T1.+Vs, T2.+Vs, wlevel_sensor_R1.Pin_1, wlevel_sensor_R2.Pin_1
  N3: Part1.D2, Lights_relay.COIL2
  N4: Part1.D3_PWM, Pump_relay.COIL2
  N5: Part1.D5_PWM, T1.GND, wlevel_sensor_R2.Pin_0
  N6: Part1.D6_PWM, T2.GND, wlevel_sensor_R1.Pin_0
  N7: Lights_relay.C, Pump_relay.C

notes:
  Pump relay
  Lights relay
  Wlevel limit
  Wlevel empty
  Temp/hum
